# Fritzing sketch sensor pir conexiones (saved by Fritzing 0.7.4b)
breadboards: 1

parts:
  Arduino1 = Arduino
  J1 = Infrared Proximity Sensor
  LED1 = LED - 5mm [color="Red (633nm)" package="5 mm [THT]"]
  R1 = Resistor [tolerance=±5% resistance=220 package=THT]

nets:
  N1: Arduino1.D8, R1.Pin_0
  N2: Arduino1.D7, J1.Vout
  N3: J1.GND, LED1.anode
  N4: LED1.cathode, R1.Pin_1

notes:
  No hay el sensor Pir de Paralax en las librerias de este soft, por favor consulten el datashet antes de conectarlo, gracias.
  BY GUILLENXT
